# Fritzing sketch Spectrum (saved by Fritzing 0.9.2b)

parts:
  J1 = male pin header, 8 pins [form="♂ (male)"]
  J2 = male pin header, 8 pins [form="♂ (male)"]
  Teensy_3_1 = Teensy 3.1
  R1 = Resistor [tolerance=±5% resistance=47k package=THT]
  R2 = Resistor [tolerance=±5% resistance=10k package=THT]
  R3 = Resistor [tolerance=±5% resistance=2.2k package=THT]
  R4 = Resistor [tolerance=±5% resistance=47k package=THT]
  C1 = Electrolytic Capacitor [capacitance=10µF voltage=10V package="100 mil [THT, electrolytic]"]
  C2 = Electrolytic Capacitor [capacitance=10µF voltage=10V package="100 mil [THT, electrolytic]"]
  J3 = Screw terminal - 2 pins [package=THT]
  JP1 = RCA [package=rca_lock]
  LED1 = LED - 5mm [color="Red (633nm)" package="5 mm [THT]"]
  R5 = Resistor [tolerance=±5% resistance=330 package=THT]
  R6 = Resistor [tolerance=±5% resistance=10k package=THT]

nets:
  N1: J1.pin1, J1.pin2, J1.pin3, J1.pin7, J1.pin8, Teensy_3_1.GND
  N2: J1.pin4, Teensy_3_1.A0/D14, R6.Pin_0
  N3: J1.pin5, Teensy_3_1.D11
  N4: J1.pin6, J2.pin6, Teensy_3_1.Vin, J3.pin2, R6.Pin_1
  N5: J2.pin1, Teensy_3_1.A2/D16
  N6: J2.pin2, Teensy_3_1.A3/D17
  N7: J2.pin3, Teensy_3_1.A5/D19
  N8: J2.pin4, Teensy_3_1.A4/D18
  N9: J2.pin5, Teensy_3_1.D9
  N10: J2.pin7, Teensy_3_1.A7/D21
  N11: J2.pin8, Teensy_3_1.D13
  N12: Teensy_3_1.A1/D15, R1.Pin_1, C2.+
  N13: Teensy_3_1.A6/D20, R5.Pin_1
  N14: Teensy_3_1.3V3, R2.Pin_1
  N15: Teensy_3_1.AGND, R4.Pin_0, JP1.PIN, LED1.cathode
  N16: R1.Pin_0, R2.Pin_0, R3.Pin_1, C1.+
  N17: R3.Pin_0, C1.-, JP1.SHELL
  N18: R4.Pin_1, C2.-, JP1.SWITCH
  N19: LED1.anode, R5.Pin_0

notes:
  Power
  Teensy Spectrum Analyser
  Nick Metcalfe 11/2015
  Audio In
